// Logisim project 16_key_chromatic_piano.circ as structural Verilog: 1 circuit, main circuit main
module main (
);

  wire button_1_out, button_2_out, button_3_out, button_4_out, button_5_out, button_6_out, button_7_out,
       button_8_out, button_9_out, button_10_out, button_11_out, button_12_out, button_13_out, button_14_out,
       button_15_out, button_16_out, or_1_out;
  wire [3:0] priority_encoder_1_out;
  wire [6:0] buzzer_1_p3;
  wire [13:0] multiplexer_1_out;

  Button button_1 (.out(button_1_out));
  Button button_2 (.out(button_2_out));
  Button button_3 (.out(button_3_out));
  Button button_4 (.out(button_4_out));
  Button button_5 (.out(button_5_out));
  Button button_6 (.out(button_6_out));
  Button button_7 (.out(button_7_out));
  Button button_8 (.out(button_8_out));
  Multiplexer #(.select(4), .width(14)) multiplexer_1 (
    .in0(14'hdc), .in1(14'he9), .in2(14'hf7), .in3(14'h106), .in4(14'h115), .in5(14'h126), .in6(14'h137),
    .in7(14'h14a), .in8(14'h15d), .in9(14'h172), .in10(14'h188), .in11(14'h19f), .in12(14'h1b8),
    .in13(14'h1d2), .in14(14'h1ee), .in15(14'h20b), .out(multiplexer_1_out), .sel(priority_encoder_1_out));
  Priority_Encoder #(.select(4)) priority_encoder_1 (
    .in0(button_2_out), .in1(button_1_out), .in2(button_8_out), .in3(button_5_out), .in4(button_3_out),
    .in5(button_6_out), .in6(button_4_out), .in7(button_7_out), .in8(button_12_out), .in9(button_9_out),
    .in10(button_13_out), .in11(button_10_out), .in12(button_14_out), .in13(button_11_out),
    .in14(button_15_out), .in15(button_16_out), .out(priority_encoder_1_out));
  Button button_9 (.out(button_9_out));
  Button button_10 (.out(button_10_out));
  Button button_11 (.out(button_11_out));
  Button button_12 (.out(button_12_out));
  Button button_13 (.out(button_13_out));
  Button button_14 (.out(button_14_out));
  Button button_15 (.out(button_15_out));
  Button button_16 (.out(button_16_out));
  or or_1 (or_1_out, button_2_out, button_1_out, button_8_out, button_5_out, button_3_out, button_6_out, button_4_out, button_7_out, button_12_out, button_9_out, button_13_out, button_10_out, button_14_out, button_11_out, button_15_out, button_16_out);
  // Buzzer #(.waveform("Square")) buzzer_1: pin names not known; wires that end beside it: multiplexer_1_out, or_1_out, buzzer_1_p3
  Slider #(.width(7)) slider_1 (.out(buzzer_1_p3));
endmodule
