// Logisim project simple_piano.circ as structural Verilog: 1 circuit, main circuit main
module main (
);

  wire button_1_out, button_2_out, button_3_out, button_4_out, button_5_out, button_6_out, button_7_out,
       button_8_out, or_1_out;
  wire [2:0] priority_encoder_1_out;
  wire [13:0] multiplexer_1_out;

  Button button_1 (.out(button_1_out));
  Button button_2 (.out(button_2_out));
  Button button_3 (.out(button_3_out));
  Button button_4 (.out(button_4_out));
  Multiplexer #(.select(3), .width(14)) multiplexer_1 (
    .in0(14'h106), .in1(14'h126), .in2(14'h14a), .in3(14'h15d), .in4(14'h188), .in5(14'h1b8), .in6(14'h1ee),
    .in7(14'h20b), .out(multiplexer_1_out), .sel(priority_encoder_1_out));
  Priority_Encoder priority_encoder_1 (
    .in0(button_4_out), .in1(button_1_out), .in2(button_2_out), .in3(button_3_out), .in4(button_5_out),
    .in5(button_6_out), .in6(button_7_out), .in7(button_8_out), .out(priority_encoder_1_out));  // open: en_in
  Button button_5 (.out(button_5_out));
  Button button_6 (.out(button_6_out));
  Button button_7 (.out(button_7_out));
  Button button_8 (.out(button_8_out));
  or or_1 (or_1_out, button_4_out, button_1_out, button_2_out, button_3_out, button_5_out, button_6_out, button_7_out, button_8_out);
  // Buzzer #(.waveform("Square")) buzzer_1: pin names not known; wires that end beside it: multiplexer_1_out, or_1_out, {7{1'b1}}
endmodule
